# Fritzing sketch Password (saved by Fritzing 0.9.2b)
circuit board: 8.61032cm x 3.01934cm
breadboards: 1

parts:
  X1 = USB Connectors [package=usb-a-h]
  R9 = Resistor [tolerance=±5% resistance=68 package=THT]
  R10 = Resistor [tolerance=±5% resistance=68 package=THT]
  S1 = Round Pushbutton
  R5 = Resistor [tolerance=±5% resistance=1k package=THT]
  Q2 = PNP-Transistor [part_number=BC327 package="TO92 [THT]"]
  Q1 = PNP-Transistor [part_number=BC327 package="TO92 [THT]"]
  Q3 = PNP-Transistor [part_number=BC327 package="TO92 [THT]"]
  Q4 = PNP-Transistor [part_number=BC327 package="TO92 [THT]"]
  IC3 = ULN2803A [package=THT]
  U1 = 7-SEGMENT-4DIGIT-YOUNGSUN [package=7-segment-4digit-youngsun-longpads]
  R11 = Resistor [tolerance=±5% resistance=1.5k package=THT]
  R4 = Resistor [tolerance=±5% resistance=1k package=THT]
  D2 = Zener Diode [part_number=1N4732A breakdown_voltage=3.6V package="300 mil [THT]"]
  R6 = Resistor [tolerance=±5% resistance=1k package=THT]
  R7 = Resistor [tolerance=±5% resistance=1k package=THT]
  D1 = Zener Diode [part_number=1N4732A breakdown_voltage=3.6V package="300 mil [THT]"]
  IC1 = ATTiny2313 [part_number="ATtiny 2313" package=THT]
  XTAL1 = Crystal [frequency="16 MHz" package=THT]
  C2 = Ceramic Capacitor [capacitance=100nF package="100 mil [THT, multilayer]"]
  C1 = Ceramic Capacitor [capacitance=100nF voltage=6.3V package="100 mil [THT, multilayer]"]

nets (from the schematic view):
  N1: X1.D-, R10.Pin_1, R11.Pin_0, D2.cathode
  N2: X1.D+, R9.Pin_1, D1.cathode
  5V: X1.VBUS, Q2.E, Q1.E, Q3.E, Q4.E, R11.Pin_1, IC1.VCC
  GND: X1.GND, S1.leg0, IC3.0V, D2.anode, D1.anode, IC1.GND, C2.1, C1.1
  N3: R9.Pin_0, IC1.PD4
  N4: R10.Pin_0, IC1.PD3
  N5: S1.leg1, IC1.PD5
  N6: R5.Pin_0, IC1.PD0
  N7: R5.Pin_1, Q2.B
  N8: Q2.C, U1.DIG2
  N9: Q1.B, R4.Pin_1
  N10: Q1.C, U1.DIG1
  N11: Q3.B, R6.Pin_1
  N12: Q3.C, U1.DIG3
  N13: Q4.B, R7.Pin_1
  N14: Q4.C, U1.DIG4
  N15: IC3.In_1, IC1.PB6
  N16: IC3.In_2, IC1.PB5
  N17: IC3.In_3, IC1.PB4
  N18: IC3.In_4, IC1.PB3
  N19: IC3.In_5, IC1.PB2
  N20: IC3.In_6, IC1.PB1
  N21: IC3.In_7, IC1.PB0
  N22: IC3.In_8, IC1.PD6
  N23: IC3.Out_8, U1.DP
  N24: IC3.Out_7, U1.B
  N25: IC3.Out_6, U1.G
  N26: IC3.Out_5, U1.A
  N27: IC3.Out_4, U1.C
  N28: IC3.Out_3, U1.F
  N29: IC3.Out_2, U1.E
  N30: IC3.Out_1, U1.D
  N31: R4.Pin_0, IC1.PB7
  N32: R6.Pin_0, IC1.PD1
  N33: R7.Pin_0, IC1.PD2
  N34: IC1.PA1, XTAL1.pin_1, C1.0
  N35: IC1.PA0, XTAL1.pin_0, C2.0

notes:
  Password Storage, A deniable storage for 16 passwords with hardware PIN and USB-HID, 1
